# Fritzing sketch blinkled (saved by Fritzing 0.7.4b)
breadboards: 1

parts:
  BeagleBone1 = beaglebone-a5
  R1 = Resistor [tolerance=±5% resistance=1k package=THT]
  LED1 = LED - 5mm [color="Red (633nm)" package="5 mm [THT]"]
  ALD1 = ALD1106 Quad N-channel MOSFET  # not connected

nets:
  N1: BeagleBone1.connectorp8-1, R1.Pin_0
  N2: BeagleBone1.connectorp8-3, LED1.anode
  N3: R1.Pin_1, LED1.cathode

custom parts:
  ALD1106 Quad N-channel MOSFET: Quad N-channel MOSFET
