# Fritzing sketch bmp085 (saved by Fritzing 0.7.4b)

parts:
  Part1 = Barometric Pressure Sensor - BMP085 Breakout  # not connected
  Part2 = Barometric Pressure Sensor - BMP085 Breakout
  BeagleBone1 = beaglebone-a5

nets:
  N1: Part2.VCC, BeagleBone1.connectorp9-3
  N2: Part2.GND, BeagleBone1.connectorp9-2
  N3: Part2.SCL, BeagleBone1.connectorp9-17
  N4: Part2.SDA, BeagleBone1.connectorp9-18
