# Fritzing sketch oscon (saved by Fritzing 0.7.4b)
breadboards: 1

parts:
  BeagleBone1 = beaglebone-a5
  R1 = Resistor [tolerance=±5% resistance=1k package=THT]
  LED1 = LED - 5mm [color="Red (633nm)" package="5 mm [THT]"]
  R2 = Trimmer Potentiometer [maximum_resistance=10kΩ package=THT]
  R3 = Resistor [tolerance=±5% resistance=1k package=THT]

nets:
  N1: BeagleBone1.connectorp8-1, R1.Pin_0
  N2: BeagleBone1.connectorp8-3, R3.Pin_1
  N3: BeagleBone1.connectorp8-5, R3.Pin_0
  N4: BeagleBone1.connectorp8-13, LED1.anode
  N5: BeagleBone1.connectorp9-32, R2.leg1
  N6: BeagleBone1.connectorp9-34, R2.leg2
  N7: BeagleBone1.connectorp9-36, R2.wiper
  N8: R1.Pin_1, LED1.cathode
