# Fritzing sketch pot (saved by Fritzing 0.7.4b)

parts:
  R1 = Trimmer Potentiometer [maximum_resistance=10kΩ package=THT]
  BeagleBone1 = beaglebone-a5

nets:
  N1: R1.leg1, BeagleBone1.connectorp9-34
  N2: R1.wiper, BeagleBone1.connectorp9-36
  N3: R1.leg2, BeagleBone1.connectorp9-32
